# Fritzing sketch DHT (saved by Fritzing 0.9.3b)

parts:
  Bauteil1 = Arduino Uno (Rev3)
  LCD1 = LCD screen  # not connected
  T1 = TMP36 Temperature Sensor [package="TO92 [THT]"]

nets:
  N1: Bauteil1.D3_PWM, T1.+Vs
  N2: Bauteil1.5V, T1.Vout
  GND: Bauteil1.GND, T1.GND
