# Fritzing sketch fadeSchaltplan (saved by Fritzing 0.9.3b)
breadboards: 1

parts:
  Bauteil1 = Arduino Uno (Rev3)
  S1 = Pushbutton [package="[THT]"]
  S2 = Pushbutton [package="[THT]"]
  S3 = Pushbutton [package="[THT]"]
  LED1 = LED - 5mm [color="Red (633nm)" package="5 mm [THT]"]
  R1 = Resistor [tolerance=±5% resistance=220 package=THT]
  R2 = Resistor [tolerance=±5% resistance=220 package=THT]
  LED2 = LED - 5mm [color="Red (633nm)" package="5 mm [THT]"]
  LED3 = LED - 5mm [color="Red (633nm)" package="5 mm [THT]"]
  R3 = Resistor [tolerance=±5% resistance=220 package=THT]
  R4 = Resistor [tolerance=±5% resistance=220 package=THT]
  R5 = Resistor [tolerance=±5% resistance=220 package=THT]
  R6 = Resistor [tolerance=±5% resistance=220 package=THT]

nets:
  N1: Bauteil1.D11_PWM/MOSI, R5.Pin_0
  N2: Bauteil1.D12/MISO, R3.Pin_0
  N3: Bauteil1.D13/SCK, R1.Pin_0
  N4: Bauteil1.D2, S1.Pin_1, S1.Pin_2, R2.Pin_1
  N5: Bauteil1.D3_PWM, S2.Pin_1, S2.Pin_2, R4.Pin_1
  N6: Bauteil1.D4, S3.Pin_1, S3.Pin_2, R6.Pin_1
  N7: Bauteil1.5V, S1.Pin_3, S1.Pin_4, S2.Pin_3, S2.Pin_4, S3.Pin_3, S3.Pin_4
  N8: Bauteil1.GND, R2.Pin_0, R4.Pin_0, R6.Pin_0
  N9: LED1.anode, R1.Pin_1
  N10: LED2.anode, R3.Pin_1
  N11: LED3.anode, R5.Pin_1
